# Fritzing sketch Buggytracker (saved by Fritzing 0.9.1b)
breadboards: 1

parts:
  S1 = Reed switch [package=THT]
  Bauteil2 = Memoire 1.0 - SD card log shield
  R2 = Resistor [tolerance=±5% resistance=10k package=THT]
  Bauteil1 = Arduino Leonardo (Rev3b) [part_number="Blend "]
  BAT1 = BC9VPC [package=bc9vpc]
  Power_plug1 = Power plug
  Bauteil3 = Real Time Clock Module - DS1307 RTC Breakout Board

nets:
  N1: S1.pin_1, Bauteil2.DIG_1, R2.Pin_1, Bauteil1.D1/TX
  GND: S1.pin_2, Bauteil2.GND, Bauteil1.GND
  N2: Bauteil2.DIG_12, Bauteil1.D12/A11
  +5V: Bauteil2.+5V, R2.Pin_0, Bauteil1.5V
  N3: Bauteil2.N$29, Bauteil2.N$41
  N4: Bauteil1.SDA, Bauteil3.SDA
  N5: Bauteil1.SCL, Bauteil3.SCL
  N6: BAT1.V+, Power_plug1.GND
  N7: BAT1.V-, Power_plug1.VCC
